// Logisim project ping-pong.circ as structural Verilog
// 0xd
module movePoint (
  output out_1,
  output out_2,
  output out_3,
  output out_4
);

  wire and_1_out, and_2_out, bot_enabled, comp_y_cord_1_out_4, comp_y_cord_2_out_4, comparator_5_eq,
       comparator_6_eq, comparator_7_eq, comparator_8_eq, comparator_9_eq, comparator_10_eq,
       comparator_11_eq, comparator_12_eq, comparator_14_eq, d_ff_2_q, d_ff_5_q, fail1, fail2,
       frequency_divider_1_out, frequency_divider_2_out, frequency_divider_4_out, frequency_divider_5_out,
       gameover, isDown, kpower, l_button, lose, not_1_out, not_2_out, not_3_out, not_4_out, not_5_out,
       not_6_out, not_7_out, o_button, or_2_out, or_3_out, or_4_out, or_6_out, or_7_out, or_16_out,
       or_17_out, or_18_out, or_19_out, or_21_out, or_22_out, or_23_out, or_24_out, pause, playing, power,
       pull_resistor_2_node, restart, s_button, swap_x_direction_left_wall, swap_x_direction_right_wall,
       t_ff_1_q, transistor_1_out, w_button;
  wire [3:0] counter_1_q, counter_3_q, counter_4_q;
  wire [4:0] dmx_x_cord;
  wire [6:0] keyboard;
  wire [7:0] multiplexer_34_out, p1_score_bin, p2_score_bin;
  wire [11:0] p1_score, p2_score;
  wire [14:1] decoder_3_out0, middle_rocket_pixel_left;
  wire [15:0] bot, cord1, cord2, D0, D1, D3, D4, D5, D6, D7, D8, D9, D10, D11, D12, D13, D14, D15, D16, D17,
       D18, D19, D20, D21, D22, D23, D24, D25, D26, D27, D28, D30, D31, demultiplexer_1_out1,
       demultiplexer_1_out30, dmx_y_cord, n0, n1, n2, n3, n4, n5, n6, n7, n8, n9, n10, n11, n12, n13, n14,
       n15, n16, n17, n18, n19, n20, n21, n22, n23, n24, n25, n26, n27, n28, n29, n30, n31, player1, player2,
       racket2, shifter_1_out, shifter_2_out, shifter_3_out, shifter_4_out, shifter_5_out, shifter_6_out,
       undriven, undriven_2, undriven_3, undriven_4, undriven_5, undriven_6, undriven_7, undriven_8,
       undriven_9, undriven_10, undriven_11, undriven_12, undriven_13, undriven_14, undriven_15, undriven_16,
       undriven_17, undriven_18, undriven_19, undriven_20, undriven_21, undriven_22, undriven_23,
       undriven_24, undriven_25, undriven_26, undriven_27, undriven_28, undriven_29, undriven_30,
       undriven_31, undriven_32, undriven_33, undriven_34, undriven_35, undriven_36, undriven_37,
       undriven_38, undriven_39, undriven_40, undriven_41, undriven_42, undriven_43, undriven_44,
       undriven_45, undriven_46, undriven_47, undriven_48, undriven_49, undriven_50, undriven_51,
       undriven_52, undriven_53, undriven_54, undriven_55, undriven_56, undriven_57, undriven_58,
       undriven_59, undriven_60, undriven_61, undriven_62, undriven_63, undriven_64;

  Hex_Digit_Display hex_digit_display_1 (.value(p1_score[7:4]));  // open: dp
  Hex_Digit_Display hex_digit_display_2 (.value(p1_score[11:8]));  // open: dp
  Hex_Digit_Display hex_digit_display_3 (.value(p1_score[3:0]));  // open: dp
  DotMatrix #(.matrixcols(32), .matrixrows(16)) dotmatrix_1 (
    .col0(n0), .col1(n1), .col2(n2), .col3(n3), .col4(n4), .col5(n5), .col6(n6), .col7(n7), .col8(n8),
    .col9(n9), .col10(n10), .col11(n11), .col12(n12), .col13(n13), .col14(n14), .col15(n15), .col16(n16),
    .col17(n17), .col18(n18), .col19(n19), .col20(n20), .col21(n21), .col22(n22), .col23(n23), .col24(n24),
    .col25(n25), .col26(n26), .col27(n27), .col28(n28), .col29(n29), .col30(n30), .col31(n31));
  Keyboard #(.buflen(1)) keyboard_1 (.clk(kpower), .data(keyboard));  // open: re, clr, avail
  Hex_Digit_Display hex_digit_display_4 (.value(p2_score[7:4]));  // open: dp
  Hex_Digit_Display hex_digit_display_5 (.value(p2_score[11:8]));  // open: dp
  Hex_Digit_Display hex_digit_display_6 (.value(p2_score[3:0]));  // open: dp
  D_Flip_Flop d_ff_1 (.Q(isDown), .preset(dmx_y_cord[15]), .reset(dmx_y_cord[0]));  // open: clk, D, Qn, en
  Counter #(.width(4), .max('hf)) counter_1 (
    .load(isDown), .Q(counter_1_q), .clk(power));  // open: D, count, carry, clr
  Multiplexer #(.width(16)) multiplexer_1 (.in0(player2), .in1(bot), .out(racket2), .sel(bot_enabled));  // open: en
  // Probe on keyboard
  // Probe on keyboard
  // Probe on keyboard
  // Probe on keyboard
  Decoder #(.select(4)) decoder_1 (
    .out0(dmx_y_cord[0]), .out1(dmx_y_cord[1]), .out2(dmx_y_cord[2]), .out3(dmx_y_cord[3]),
    .out4(dmx_y_cord[4]), .out5(dmx_y_cord[5]), .out6(dmx_y_cord[6]), .out7(dmx_y_cord[7]),
    .out8(dmx_y_cord[8]), .out9(dmx_y_cord[9]), .out10(dmx_y_cord[10]), .out11(dmx_y_cord[11]),
    .out12(dmx_y_cord[12]), .out13(dmx_y_cord[13]), .out14(dmx_y_cord[14]), .out15(dmx_y_cord[15]),
    .sel(counter_1_q));  // open: en
  // Probe on d_ff_2_q
  D_Flip_Flop d_ff_2 (
    .Q(d_ff_2_q), .preset(swap_x_direction_right_wall), .reset(swap_x_direction_left_wall));  // open: clk, D, Qn, en
  assign D1 = player1 | demultiplexer_1_out1;  // OR_Gate or_1, 16 bits wide
  Comparator #(.width(7)) comparator_1 (.a(keyboard), .b(7'b1110111), .eq(w_button));  // open: gt, lt
  Comparator #(.width(7)) comparator_2 (.a(keyboard), .b(7'b1110011), .eq(s_button));  // open: gt, lt
  Comparator #(.width(7)) comparator_3 (.a(keyboard), .b(7'b1101111), .eq(o_button));  // open: gt, lt
  Comparator #(.width(7)) comparator_4 (.a(keyboard), .b(7'b1101100), .eq(l_button));  // open: gt, lt
  Counter #(.width(5), .max('h1f)) counter_2 (
    .load(d_ff_2_q), .Q(dmx_x_cord), .clk(power), .clr(or_2_out));  // open: D, count, carry
  buf or_2 (or_2_out, restart);  // OR_Gate
  Shifter #(.width(16)) shifter_1 (.in(dmx_y_cord), .\dist (4'b0001), .out(shifter_1_out));
  Shifter #(.width(16), .shift("lr")) shifter_2 (.in(dmx_y_cord), .\dist (4'b0001), .out(shifter_2_out));
  Multiplexer #(.select(2), .width(16), .enable("false")) multiplexer_2 (
    .in0(undriven), .in1(D0), .in2(undriven_9), .in3({16{1'b0}}), .out(n0), .sel({pause, playing}));
  Multiplexer #(.select(2), .width(16), .enable("false")) multiplexer_3 (
    .in0(undriven_2), .in1(D4), .in2(undriven_10), .in3(16'h1100), .out(n4), .sel({pause, playing}));
  Multiplexer #(.select(2), .width(16), .enable("false")) multiplexer_4 (
    .in0(undriven_3), .in1(D8), .in2(undriven_11), .in3(16'hfc), .out(n8), .sel({pause, playing}));
  Multiplexer #(.select(2), .width(16), .enable("false")) multiplexer_5 (
    .in0(undriven_4), .in1(D12), .in2(undriven_12), .in3({16{1'b0}}), .out(n12), .sel({pause, playing}));
  Multiplexer #(.select(2), .width(16), .enable("false")) multiplexer_6 (
    .in0(undriven_5), .in1(D16), .in2(undriven_13), .in3(16'h1f8), .out(n16), .sel({pause, playing}));
  Multiplexer #(.select(2), .width(16), .enable("false")) multiplexer_7 (
    .in0(undriven_6), .in1(D20), .in2(undriven_14), .in3(16'h124), .out(n20), .sel({pause, playing}));
  Multiplexer #(.select(2), .width(16), .enable("false")) multiplexer_8 (
    .in0(undriven_7), .in1(D24), .in2(undriven_15), .in3(16'h124), .out(n24), .sel({pause, playing}));
  Multiplexer #(.select(2), .width(16), .enable("false")) multiplexer_9 (
    .in0(undriven_8), .in1(D28), .in2(undriven_16), .in3(16'h1fe4), .out(n28), .sel({pause, playing}));
  or or_3 (or_3_out, l_button, restart);
  or or_4 (or_4_out, o_button, restart, l_button);
  assign bot = shifter_1_out | dmx_y_cord | shifter_2_out;  // OR_Gate or_5, 16 bits wide
  Demultiplexer #(.select(5), .width(16)) demultiplexer_1 (
    .out0(D0), .out1(demultiplexer_1_out1), .out2(cord1), .out3(D3), .out4(D4), .out5(D5), .out6(D6),
    .out7(D7), .out8(D8), .out9(D9), .out10(D10), .out11(D11), .out12(D12), .out13(D13), .out14(D14),
    .out15(D15), .out16(D16), .out17(D17), .out18(D18), .out19(D19), .out20(D20), .out21(D21), .out22(D22),
    .out23(D23), .out24(D24), .out25(D25), .out26(D26), .out27(D27), .out28(D28), .out29(cord2),
    .out30(demultiplexer_1_out30), .out31(D31), .in(dmx_y_cord), .sel(dmx_x_cord));  // open: en
  or or_6 (or_6_out, s_button, restart);
  not not_1 (not_1_out, restart);
  or or_7 (or_7_out, w_button, restart, s_button);
  Counter #(.width(4), .max('hd), .ongoal("stay")) counter_3 (
    .load(or_3_out), .D(4'b0111), .count(not_2_out), .Q(counter_3_q), .clk(or_4_out));  // open: carry, clr
  not not_2 (not_2_out, restart);
  Multiplexer #(.select(2), .width(16), .enable("false")) multiplexer_10 (
    .in0(undriven_17), .in1(D1), .in2(undriven_25), .in3({16{1'b0}}), .out(n1), .sel({pause, playing}));
  Multiplexer #(.select(2), .width(16), .enable("false")) multiplexer_11 (
    .in0(undriven_18), .in1(D5), .in2(undriven_26), .in3(16'h1100), .out(n5), .sel({pause, playing}));
  Multiplexer #(.select(2), .width(16), .enable("false")) multiplexer_12 (
    .in0(undriven_19), .in1(D9), .in2(undriven_27), .in3(16'h110), .out(n9), .sel({pause, playing}));
  Multiplexer #(.select(2), .width(16), .enable("false")) multiplexer_13 (
    .in0(undriven_20), .in1(D13), .in2(undriven_28), .in3(16'h1f8), .out(n13), .sel({pause, playing}));
  Multiplexer #(.select(2), .width(16), .enable("false")) multiplexer_14 (
    .in0(undriven_21), .in1(D17), .in2(undriven_29), .in3({16{1'b0}}), .out(n17), .sel({pause, playing}));
  Multiplexer #(.select(2), .width(16), .enable("false")) multiplexer_15 (
    .in0(undriven_22), .in1(D21), .in2(undriven_30), .in3(16'h98), .out(n21), .sel({pause, playing}));
  Multiplexer #(.select(2), .width(16), .enable("false")) multiplexer_16 (
    .in0(undriven_23), .in1(D25), .in2(undriven_31), .in3(16'h124), .out(n25), .sel({pause, playing}));
  Multiplexer #(.select(2), .width(16), .enable("false")) multiplexer_17 (
    .in0(undriven_24), .in1(cord2), .in2(undriven_32), .in3({16{1'b0}}), .out(n29), .sel({pause, playing}));
  // Probe on counter_4_q
  Counter #(.width(4), .max('hd), .ongoal("stay")) counter_4 (
    .load(or_6_out), .D(4'b0111), .count(not_1_out), .Q(counter_4_q), .clk(or_7_out));  // open: carry, clr
  Decoder #(.select(4)) decoder_2 (
    .out0(middle_rocket_pixel_left[1]), .out1(middle_rocket_pixel_left[2]),
    .out2(middle_rocket_pixel_left[3]), .out3(middle_rocket_pixel_left[4]),
    .out4(middle_rocket_pixel_left[5]), .out5(middle_rocket_pixel_left[6]),
    .out6(middle_rocket_pixel_left[7]), .out7(middle_rocket_pixel_left[8]),
    .out8(middle_rocket_pixel_left[9]), .out9(middle_rocket_pixel_left[10]),
    .out10(middle_rocket_pixel_left[11]), .out11(middle_rocket_pixel_left[12]),
    .out12(middle_rocket_pixel_left[13]), .out13(middle_rocket_pixel_left[14]), .sel(counter_4_q));  // open: out14, out15, en
  Decoder #(.select(4)) decoder_3 (
    .out0(decoder_3_out0[1]), .out1(decoder_3_out0[2]), .out2(decoder_3_out0[3]), .out3(decoder_3_out0[4]),
    .out4(decoder_3_out0[5]), .out5(decoder_3_out0[6]), .out6(decoder_3_out0[7]), .out7(decoder_3_out0[8]),
    .out8(decoder_3_out0[9]), .out9(decoder_3_out0[10]), .out10(decoder_3_out0[11]),
    .out11(decoder_3_out0[12]), .out12(decoder_3_out0[13]), .out13(decoder_3_out0[14]), .sel(counter_3_q));  // open: out14, out15, en
  // Probe on racket2
  // Probe on player1
  assign D30 = racket2 | demultiplexer_1_out30;  // OR_Gate or_8, 16 bits wide
  Multiplexer #(.select(2), .width(16), .enable("false")) multiplexer_18 (
    .in0(undriven_33), .in1(cord1), .in2(undriven_42), .in3({16{1'b0}}), .out(n2), .sel({pause, playing}));
  Multiplexer #(.select(2), .width(16), .enable("false")) multiplexer_19 (
    .in0(undriven_34), .in1(D6), .in2(undriven_43), .in3(16'h1100), .out(n6), .sel({pause, playing}));
  Multiplexer #(.select(2), .width(16), .enable("false")) multiplexer_20 (
    .in0(undriven_35), .in1(D10), .in2(undriven_44), .in3(16'h110), .out(n10), .sel({pause, playing}));
  Multiplexer #(.select(2), .width(16), .enable("false")) multiplexer_21 (
    .in0(undriven_36), .in1(D14), .in2(undriven_45), .in3(16'h4), .out(n14), .sel({pause, playing}));
  Multiplexer #(.select(2), .width(16), .enable("false")) multiplexer_22 (
    .in0(undriven_37), .in1(D18), .in2(undriven_38), .in3(16'hc8), .out(n18), .sel({pause, playing}));
  Multiplexer #(.select(2), .width(16), .enable("false")) multiplexer_23 (
    .in0(undriven_39), .in1(D22), .in2(undriven_46), .in3({16{1'b0}}), .out(n22), .sel({pause, playing}));
  Multiplexer #(.select(2), .width(16), .enable("false")) multiplexer_24 (
    .in0(undriven_40), .in1(D26), .in2(undriven_47), .in3(16'h124), .out(n26), .sel({pause, playing}));
  Multiplexer #(.select(2), .width(16), .enable("false")) multiplexer_25 (
    .in0(undriven_41), .in1(D30), .in2(undriven_48), .in3({16{1'b0}}), .out(n30), .sel({pause, playing}));
  Shifter #(.width(16)) shifter_3 (.in({1'b0, middle_rocket_pixel_left, 1'b0}), .\dist (4'b0001), .out(shifter_3_out));
  Shifter #(.width(16), .shift("lr")) shifter_4 (
    .in({1'b0, middle_rocket_pixel_left, 1'b0}), .\dist (4'b0001), .out(shifter_4_out));
  Shifter #(.width(16)) shifter_5 (.in({1'b0, decoder_3_out0, 1'b0}), .\dist (4'b0001), .out(shifter_5_out));
  Shifter #(.width(16), .shift("lr")) shifter_6 (
    .in({1'b0, decoder_3_out0, 1'b0}), .\dist (4'b0001), .out(shifter_6_out));
  not not_3 (not_3_out, swap_x_direction_right_wall);
  Comparator #(.width(5)) comparator_5 (.a(dmx_x_cord), .b(5'b11101), .eq(comparator_5_eq));  // open: gt, lt
  not not_4 (not_4_out, swap_x_direction_left_wall);
  Comparator #(.width(5)) comparator_6 (.a(dmx_x_cord), .b({5{1'b0}}), .eq(comparator_6_eq));  // open: gt, lt
  Comparator #(.width(5)) comparator_7 (.a(dmx_x_cord), .b(5'b11101), .eq(comparator_7_eq));  // open: gt, lt
  not not_5 (not_5_out, swap_x_direction_right_wall);
  Comparator #(.width(5)) comparator_8 (.a(dmx_x_cord), .b({5{1'b0}}), .eq(comparator_8_eq));  // open: gt, lt
  not not_6 (not_6_out, swap_x_direction_left_wall);
  Comparator #(.mode("unsigned")) comparator_9 (.a(p1_score_bin), .b(8'h2), .eq(comparator_9_eq));  // open: gt, lt
  Comparator #(.mode("unsigned")) comparator_10 (.a(8'h2), .b(p2_score_bin), .eq(comparator_10_eq));  // open: gt, lt
  assign player1 = shifter_3_out | {1'b0, middle_rocket_pixel_left, 1'b0} | shifter_4_out;  // OR_Gate or_9, 16 bits wide
  assign player2 = shifter_5_out | {1'b0, decoder_3_out0, 1'b0} | shifter_6_out;  // OR_Gate or_10, 16 bits wide
  comp_y_cord comp_y_cord_1 (.in_1(racket2), .in_2(cord2), .in_3(isDown), .out_4(comp_y_cord_1_out_4));
  comp_y_cord comp_y_cord_2 (.in_1(player1), .in_2(cord1), .in_3(isDown), .out_4(comp_y_cord_2_out_4));
  and and_1 (and_1_out, not_3_out, comparator_5_eq);
  and and_2 (and_2_out, not_4_out, comparator_6_eq);
  Transistor #(.\type ("n")) transistor_1 (.in(not_5_out), .out(transistor_1_out), .gate(comparator_7_eq));
  Pull_Resistor pull_resistor_1 (.node(transistor_1_out));
  Pull_Resistor pull_resistor_2 (.node(pull_resistor_2_node));
  Transistor #(.\type ("n")) transistor_2 (.in(not_6_out), .out(pull_resistor_2_node), .gate(comparator_8_eq));
  or or_11 (gameover, comparator_9_eq, comparator_10_eq);
  Multiplexer #(.select(2), .width(16), .enable("false")) multiplexer_26 (
    .in0(undriven_49), .in1(D3), .in2(undriven_57), .in3(16'h1ffc), .out(n3), .sel({pause, playing}));
  Multiplexer #(.select(2), .width(16), .enable("false")) multiplexer_27 (
    .in0(undriven_50), .in1(D7), .in2(undriven_58), .in3(16'he00), .out(n7), .sel({pause, playing}));
  Multiplexer #(.select(2), .width(16), .enable("false")) multiplexer_28 (
    .in0(undriven_51), .in1(D11), .in2(undriven_59), .in3(16'hfc), .out(n11), .sel({pause, playing}));
  Multiplexer #(.select(2), .width(16), .enable("false")) multiplexer_29 (
    .in0(undriven_52), .in1(D15), .in2(undriven_60), .in3(16'h4), .out(n15), .sel({pause, playing}));
  Multiplexer #(.select(2), .width(16), .enable("false")) multiplexer_30 (
    .in0(undriven_53), .in1(D19), .in2(undriven_61), .in3(16'h124), .out(n19), .sel({pause, playing}));
  Multiplexer #(.select(2), .width(16), .enable("false")) multiplexer_31 (
    .in0(undriven_54), .in1(D23), .in2(undriven_62), .in3(16'h1fc), .out(n23), .sel({pause, playing}));
  Multiplexer #(.select(2), .width(16), .enable("false")) multiplexer_32 (
    .in0(undriven_55), .in1(D27), .in2(undriven_63), .in3({16{1'b0}}), .out(n27), .sel({pause, playing}));
  Multiplexer #(.select(2), .width(16), .enable("false")) multiplexer_33 (
    .in0(undriven_56), .in1(D31), .in2(undriven_64), .in3({16{1'b0}}), .out(n31), .sel({pause, playing}));
  or or_12 (swap_x_direction_right_wall, comp_y_cord_1_out_4, fail2);
  or or_13 (swap_x_direction_left_wall, comp_y_cord_2_out_4, fail1);
  // OR_Gate or_14 has open pins: in0=and_1_out, in1=and_2_out, out=open
  or or_15 (lose, transistor_1_out, pull_resistor_2_node);
  // Probe on keyboard
  // Probe on keyboard
  // Probe on keyboard
  Comparator #(.width(7)) comparator_11 (.a(keyboard), .b(7'b0100000), .eq(comparator_11_eq));  // open: gt, lt
  Comparator #(.width(7)) comparator_12 (.a(keyboard), .b(7'b1110000), .eq(comparator_12_eq));  // open: gt, lt
  Comparator #(.width(7)) comparator_13 (.a(keyboard), .b(7'b1110010), .eq(restart));  // open: gt, lt
  frequency_divider frequency_divider_1 (.IN(kpower), .OUT(frequency_divider_1_out), .n(8'h30), ._0(or_16_out));
  or or_16 (or_16_out, w_button, frequency_divider_1_out);
  frequency_divider frequency_divider_2 (.IN(kpower), .OUT(frequency_divider_2_out), .n(8'h30), ._0(or_17_out));
  or or_17 (or_17_out, s_button, frequency_divider_2_out);
  T_Flip_Flop t_ff_1 (.clk(comparator_12_eq), .T(comparator_12_eq), .Q(t_ff_1_q));  // open: Qn, preset, reset, en
  Clock clock_1 (.out(kpower));
  D_Flip_Flop d_ff_3 (.clk(w_button), .D(w_button), .Q(out_1), .reset(or_18_out));  // open: Qn, preset, en
  or or_18 (or_18_out, frequency_divider_1_out, s_button);
  D_Flip_Flop d_ff_4 (.clk(s_button), .D(s_button), .Q(out_3), .reset(or_19_out));  // open: Qn, preset, en
  or or_19 (or_19_out, frequency_divider_2_out, w_button);
  not not_7 (not_7_out, gameover);
  and and_3 (playing, not_7_out, d_ff_5_q);
  D_Flip_Flop d_ff_5 (
    .clk(comparator_11_eq), .D(comparator_11_eq), .Q(d_ff_5_q), .reset(restart));  // open: Qn, preset, en
  // Probe on keyboard
  // Probe on dmx_x_cord
  Counter #(.ongoal("continue")) counter_5 (
    .Q(p2_score_bin), .clk(fail1), .clr(restart));  // open: load, D, count, carry
  Counter #(.ongoal("continue")) counter_6 (
    .Q(p1_score_bin), .clk(fail2), .clr(restart));  // open: load, D, count, carry
  or or_20 (pause, t_ff_1_q, gameover);
  nor nor_1 (fail1, dmx_x_cord[0], dmx_x_cord[1], dmx_x_cord[2], dmx_x_cord[3], dmx_x_cord[4]);
  and and_4 (fail2, dmx_x_cord[0], dmx_x_cord[1], dmx_x_cord[2], dmx_x_cord[3], dmx_x_cord[4]);
  bcd bcd_1 (._8bit_Input(p2_score_bin), .BCD_Output(p2_score));
  bcd bcd_2 (._8bit_Input(p1_score_bin), .BCD_Output(p1_score));
  Multiplexer #(.width(8)) multiplexer_34 (
    .in0(8'h30), .in1({8{1'b0}}), .out(multiplexer_34_out), .sel(pause));  // open: en
  frequency_divider frequency_divider_3 (.IN(kpower), .OUT(power), .n(multiplexer_34_out));  // open: _0
  T_Flip_Flop t_ff_2 (.clk(comparator_14_eq), .T(comparator_14_eq), .Q(bot_enabled));  // open: Qn, preset, reset, en
  Comparator #(.width(7)) comparator_14 (.a(keyboard), .b(7'b1100010), .eq(comparator_14_eq));  // open: gt, lt
  D_Flip_Flop d_ff_6 (.clk(o_button), .D(o_button), .Q(out_2), .reset(or_21_out));  // open: Qn, preset, en
  or or_21 (or_21_out, frequency_divider_4_out, l_button);
  frequency_divider frequency_divider_4 (.IN(kpower), .OUT(frequency_divider_4_out), .n(8'h30), ._0(or_22_out));
  or or_22 (or_22_out, o_button, frequency_divider_4_out);
  D_Flip_Flop d_ff_7 (.clk(l_button), .D(l_button), .Q(out_4), .reset(or_23_out));  // open: Qn, preset, en
  or or_23 (or_23_out, frequency_divider_5_out, o_button);
  frequency_divider frequency_divider_5 (.IN(kpower), .OUT(frequency_divider_5_out), .n(8'h30), ._0(or_24_out));
  or or_24 (or_24_out, l_button, frequency_divider_5_out);

  // Other names for the same wires on the sheet: D2[15:0] = cord1; D29[15:0] = cord2; racket1[15:0] = player1;
  //   tunnel[1:0] = {pause, playing}

  // Notes on the sheet:
  //   TO-DO
  //   SCORE
  //   Player 1
  //   Intigrate CDM-8
  //   Inverse pause screan
  //   Inputs
  //   Player 1 - W and S
  //   Player 2 - O and L
  //   Pause - P
  //   Restart - R
  //   Bot - B
  //   Start game - SPACE
  //   SCORE
  //   Player 2
  //   PLAYER_1
  //   PLAYER_2
  //   движение по оси y
  //   движение по оси x
  //   BOT (Skynet in future)
  //   Playing scene
  //   Scene select
  //   00 - start scene
  //   01 - playing scene
  //   10 - gameover scene
  //   11 - pause scene
  //   Keyboard input
  //   Keyboard input
  //   можно воткнуть сюда регистр
  //   Gameover check
  //   если попадание: правая стенка
  //   если попадание: левая стенка
  //   неработающие варианты проверки на столкновение
  //   Keyboard input
  //   Запоминание последней кнопки
  //   Goal check
  //   Score count and print
  //   Power
endmodule

// ||
module comp_y_cord (
  input  [15:0] in_1,
  input  [15:0] in_2,
  input  in_3,
  output out_4
);

  wire and_1_out, and_2_out, and_3_out, and_4_out, and_5_out, and_6_out, and_7_out, and_8_out, and_9_out,
       and_10_out, and_11_out, and_12_out, and_13_out, and_14_out, and_15_out, and_16_out, and_17_out,
       and_18_out, and_19_out, and_20_out, and_21_out, and_22_out, and_23_out, and_24_out, and_25_out,
       and_26_out, and_27_out, and_28_out, and_29_out, and_30_out, and_31_out, and_32_out, and_33_out,
       and_34_out, and_35_out, and_36_out, and_37_out, and_38_out, and_39_out, and_40_out, and_41_out,
       and_42_out, and_43_out, and_44_out, or_1_out, or_2_out, or_3_out, or_4_out, or_5_out;

  and and_1 (and_1_out, in_1[0], in_2[0]);
  and and_2 (and_2_out, in_1[1], in_2[1]);
  and and_3 (and_3_out, in_1[2], in_2[2]);
  and and_4 (and_4_out, in_1[3], in_2[3]);
  and and_5 (and_5_out, in_1[4], in_2[4]);
  and and_6 (and_6_out, in_1[5], in_2[5]);
  and and_7 (and_7_out, in_1[6], in_2[6]);
  and and_8 (and_8_out, in_1[7], in_2[7]);
  and and_9 (and_9_out, in_1[8], in_2[8]);
  and and_10 (and_10_out, in_1[9], in_2[9]);
  and and_11 (and_11_out, in_1[10], in_2[10]);
  and and_12 (and_12_out, in_1[11], in_2[11]);
  and and_13 (and_13_out, in_1[12], in_2[12]);
  and and_14 (and_14_out, in_1[13], in_2[13]);
  and and_15 (and_15_out, in_1[14], in_2[14]);
  and and_16 (and_16_out, in_1[15], in_2[15]);
  and and_17 (and_17_out, in_2[2], in_1[1]);
  and and_18 (and_18_out, in_2[3], in_1[2]);
  and and_19 (and_19_out, in_2[4], in_1[3]);
  and and_20 (and_20_out, in_2[5], in_1[4]);
  and and_21 (and_21_out, in_2[6], in_1[5]);
  and and_22 (and_22_out, in_2[7], in_1[6]);
  and and_23 (and_23_out, in_2[8], in_1[7]);
  and and_24 (and_24_out, in_2[9], in_1[8]);
  and and_25 (and_25_out, in_2[10], in_1[9]);
  and and_26 (and_26_out, in_2[11], in_1[10]);
  and and_27 (and_27_out, in_2[12], in_1[11]);
  and and_28 (and_28_out, in_2[13], in_1[12]);
  and and_29 (and_29_out, in_2[14], in_1[13]);
  and and_30 (and_30_out, in_2[15], in_1[14]);
  and and_31 (and_31_out, in_2[0], in_1[1]);
  and and_32 (and_32_out, in_2[1], in_1[2]);
  and and_33 (and_33_out, in_2[2], in_1[3]);
  and and_34 (and_34_out, in_2[3], in_1[4]);
  and and_35 (and_35_out, in_2[4], in_1[5]);
  and and_36 (and_36_out, in_2[5], in_1[6]);
  and and_37 (and_37_out, in_2[6], in_1[7]);
  and and_38 (and_38_out, in_2[7], in_1[8]);
  and and_39 (and_39_out, in_2[8], in_1[9]);
  and and_40 (and_40_out, in_2[9], in_1[10]);
  and and_41 (and_41_out, in_2[10], in_1[11]);
  and and_42 (and_42_out, in_2[11], in_1[12]);
  and and_43 (and_43_out, in_2[12], in_1[13]);
  and and_44 (and_44_out, in_2[13], in_1[14]);
  or or_1 (or_1_out, and_1_out, and_2_out, and_3_out, and_4_out, and_5_out, and_6_out, and_7_out, and_8_out, and_9_out, and_10_out, and_11_out, and_12_out, and_13_out, and_14_out, and_15_out, and_16_out);
  or or_2 (or_2_out, and_17_out, and_18_out, and_19_out, and_20_out, and_21_out, and_22_out, and_23_out, and_24_out, and_25_out, and_26_out, and_27_out, and_28_out, and_29_out);
  or or_3 (or_3_out, and_31_out, and_32_out, and_33_out, and_34_out, and_35_out, and_36_out, and_37_out, and_38_out, and_39_out, and_40_out, and_41_out, and_42_out, and_43_out, and_44_out);
  or or_4 (or_4_out, or_1_out, or_2_out);
  or or_5 (or_5_out, or_1_out, or_3_out);
  Multiplexer multiplexer_1 (.in0(or_5_out), .in1(or_4_out), .out(out_4), .sel(in_3));  // open: en

  // Other names for the same wires on the sheet: _1_down = in_3; _0 = in_2[0]; ball_cord_y[15:0] = in_2; _1 = in_2[1];
  //   _2 = in_2[2]; _3 = in_2[3]; _4 = in_2[4]; _5 = in_2[5]; _6 = in_2[6]; _7 = in_2[7]; _8 = in_2[8]; _9 = in_2[9];
  //   _10 = in_2[10]; _11 = in_2[11]; _12 = in_2[12]; _13 = in_2[13]; _14 = in_2[14]; _15 = in_2[15];
  //   rock_cord_y[15:0] = in_1

  // Notes on the sheet:
  //   ракетка
  //   шарик
  //   сверху вниз
  //   снизу вверх
endmodule

module parseScore (
  input  [7:0] in_1,
  output [3:0] out_2,
  output [3:0] out_3,
  output [3:0] out_4
);

  wire [7:0] divider_1_out, divider_2_out, multiplier_1_out, multiplier_2_out, subtractor_1_out,
       subtractor_2_out;

  // Probe on in_1
  // Probe on divider_1_out
  Divider divider_1 (.a(in_1), .b(8'ha), .out(divider_1_out));  // open: upper, rem
  Divider divider_2 (.a(divider_1_out), .b(8'ha), .out(divider_2_out));  // open: upper, rem
  Multiplier multiplier_1 (.a(divider_1_out), .b(8'ha), .out(multiplier_1_out));  // open: cin, cout
  // Probe on multiplier_1_out
  // Probe on multiplier_2_out
  Multiplier multiplier_2 (.a(divider_2_out), .b(8'ha), .out(multiplier_2_out));  // open: cin, cout
  Bit_Extender #(.out_width(4)) bit_extender_1 (.in(divider_2_out), .out(out_2));
  Subtractor subtractor_1 (.a(in_1), .b(multiplier_1_out), .out(subtractor_1_out));  // open: bin, bout
  // Probe on out_2
  // Probe on subtractor_2_out
  Subtractor subtractor_2 (.a(divider_1_out), .b(multiplier_2_out), .out(subtractor_2_out));  // open: bin, bout
  // Probe on subtractor_1_out
  Bit_Extender #(.out_width(4)) bit_extender_2 (.in(subtractor_2_out), .out(out_3));
  Bit_Extender #(.out_width(4)) bit_extender_3 (.in(subtractor_1_out), .out(out_4));

  // Notes on the sheet:
  //   OBSOLETE
  //   as of v0.1.3
endmodule

module ai_right_rocket (
  input  [15:0] in_1,
  input  [15:0] in_2
);


  // Notes on the sheet:
  //   y_cord_of_ball
  //   y_cord_of_rocket
endmodule

module test (
);

  wire comparator_1_eq, comparator_2_eq, or_1_out, power, restart;
  wire [2:0] counter_1_q;
  wire [6:0] keyboard;
  wire [7:0] demultiplexer_1_out1, demultiplexer_1_out2, demultiplexer_1_out3, demultiplexer_1_out4,
       demultiplexer_1_out5, demultiplexer_1_out6, demultiplexer_1_out7, middle_rocket_pixel_left, rocket1,
       shifter_1_out, shifter_2_out;

  Keyboard #(.buflen(1)) keyboard_1 (.clk(power), .data(keyboard));  // open: re, clr, avail
  Clock clock_1 (.out(power));
  Button button_1 (.out(restart));
  // Probe on keyboard
  // Probe on keyboard
  Comparator #(.width(7)) comparator_1 (.a(keyboard), .b(7'b1110111), .eq(comparator_1_eq));  // open: gt, lt
  Comparator #(.width(7)) comparator_2 (.a(keyboard), .b(7'b1110011), .eq(comparator_2_eq));  // open: gt, lt
  DotMatrix #(.matrixcols(8), .matrixrows(8)) dotmatrix_1 (
    .col0(rocket1), .col1(demultiplexer_1_out1), .col2(demultiplexer_1_out2), .col3(demultiplexer_1_out3),
    .col4(demultiplexer_1_out4), .col5(demultiplexer_1_out5), .col6(demultiplexer_1_out6),
    .col7(demultiplexer_1_out7));
  Demultiplexer #(.select(3), .width(8)) demultiplexer_1 (
    .out0(rocket1), .out1(demultiplexer_1_out1), .out2(demultiplexer_1_out2), .out3(demultiplexer_1_out3),
    .out4(demultiplexer_1_out4), .out5(demultiplexer_1_out5), .out6(demultiplexer_1_out6),
    .out7(demultiplexer_1_out7));  // open: in, sel, en
  Counter #(.width(3), .max('h7)) counter_1 (
    .load(comparator_2_eq), .Q(counter_1_q), .clk(or_1_out), .clr(restart));  // open: D, count, carry
  or or_1 (or_1_out, comparator_1_eq, comparator_2_eq);
  Decoder #(.select(3)) decoder_1 (
    .out0(middle_rocket_pixel_left[0]), .out1(middle_rocket_pixel_left[1]),
    .out2(middle_rocket_pixel_left[2]), .out3(middle_rocket_pixel_left[3]),
    .out4(middle_rocket_pixel_left[4]), .out5(middle_rocket_pixel_left[5]),
    .out6(middle_rocket_pixel_left[6]), .out7(middle_rocket_pixel_left[7]), .sel(counter_1_q));  // open: en
  Shifter shifter_1 (.in(middle_rocket_pixel_left), .\dist (3'b001), .out(shifter_1_out));
  Shifter #(.shift("lr")) shifter_2 (.in(middle_rocket_pixel_left), .\dist (3'b001), .out(shifter_2_out));
  assign rocket1 = shifter_1_out | middle_rocket_pixel_left | shifter_2_out;  // OR_Gate or_2, 8 bits wide

  // Notes on the sheet:
  //   Inputs
  //   w, s // o, l
endmodule

module frequency_divider (
  input  [7:0] n,
  input  IN,
  input  _0,
  output OUT
);

  wire comparator_1_eq, comparator_1_lt, or_1_out, or_2_out;
  wire [7:0] counter_1_q;

  Counter counter_1 (.count(IN), .Q(counter_1_q), .clk(IN), .clr(or_1_out));  // open: load, D, carry
  or or_1 (or_1_out, _0, or_2_out);
  Comparator #(.mode("unsigned")) comparator_1 (
    .a(n), .b(counter_1_q), .eq(comparator_1_eq), .lt(comparator_1_lt));  // open: gt
  or or_2 (or_2_out, comparator_1_eq, comparator_1_lt);
  T_Flip_Flop t_ff_1 (.clk(or_2_out), .T(or_2_out), .Q(OUT), .reset(_0));  // open: Qn, preset, en
endmodule

module bcd (
  input  [7:0] _8bit_Input,
  output [11:0] BCD_Output
);

  wire [3:0] bcd_helper_1_out, bcd_helper_2_out, bcd_helper_3_out, bcd_helper_4_out, bcd_helper_5_out,
       bcd_helper_6_out, bcd_helper_7_out, bcd_helper_8_out, bcd_helper_9_out, bcd_helper_10_out,
       bcd_helper_11_out, bcd_helper_12_out, bcd_helper_13_out, bcd_helper_14_out, bcd_helper_15_out,
       bcd_helper_16_out, bcd_helper_17_out, bcd_helper_18_out;
  wire [3:3] bcd_helper_21_out;

  // Probe on _8bit_Input
  bcd_helper bcd_helper_1 (.inp({3'b000, _8bit_Input[7]}), .out(bcd_helper_1_out));
  bcd_helper bcd_helper_2 (.inp(4'b0000), .out(bcd_helper_2_out));
  bcd_helper bcd_helper_3 (.inp(4'b0000), .out(bcd_helper_3_out));
  bcd_helper bcd_helper_4 (.inp({bcd_helper_1_out[2:0], _8bit_Input[6]}), .out(bcd_helper_4_out));
  bcd_helper bcd_helper_5 (.inp({bcd_helper_2_out[2:0], bcd_helper_1_out[3]}), .out(bcd_helper_5_out));
  bcd_helper bcd_helper_6 (.inp({bcd_helper_3_out[2:0], bcd_helper_2_out[3]}), .out(bcd_helper_6_out));
  bcd_helper bcd_helper_7 (.inp({bcd_helper_4_out[2:0], _8bit_Input[5]}), .out(bcd_helper_7_out));
  bcd_helper bcd_helper_8 (.inp({bcd_helper_5_out[2:0], bcd_helper_4_out[3]}), .out(bcd_helper_8_out));
  bcd_helper bcd_helper_9 (.inp({bcd_helper_6_out[2:0], bcd_helper_5_out[3]}), .out(bcd_helper_9_out));
  bcd_helper bcd_helper_10 (.inp({bcd_helper_7_out[2:0], _8bit_Input[4]}), .out(bcd_helper_10_out));
  bcd_helper bcd_helper_11 (.inp({bcd_helper_8_out[2:0], bcd_helper_7_out[3]}), .out(bcd_helper_11_out));
  bcd_helper bcd_helper_12 (.inp({bcd_helper_9_out[2:0], bcd_helper_8_out[3]}), .out(bcd_helper_12_out));
  bcd_helper bcd_helper_13 (.inp({bcd_helper_10_out[2:0], _8bit_Input[3]}), .out(bcd_helper_13_out));
  bcd_helper bcd_helper_14 (.inp({bcd_helper_11_out[2:0], bcd_helper_10_out[3]}), .out(bcd_helper_14_out));
  bcd_helper bcd_helper_15 (.inp({bcd_helper_12_out[2:0], bcd_helper_11_out[3]}), .out(bcd_helper_15_out));
  bcd_helper bcd_helper_16 (.inp({bcd_helper_13_out[2:0], _8bit_Input[2]}), .out(bcd_helper_16_out));
  bcd_helper bcd_helper_17 (.inp({bcd_helper_14_out[2:0], bcd_helper_13_out[3]}), .out(bcd_helper_17_out));
  bcd_helper bcd_helper_18 (.inp({bcd_helper_15_out[2:0], bcd_helper_14_out[3]}), .out(bcd_helper_18_out));
  bcd_helper bcd_helper_19 (.inp({bcd_helper_16_out[2:0], _8bit_Input[1]}), .out(BCD_Output[4:1]));
  bcd_helper bcd_helper_20 (.inp({bcd_helper_17_out[2:0], bcd_helper_16_out[3]}), .out(BCD_Output[8:5]));
  bcd_helper bcd_helper_21 (
    .inp({bcd_helper_18_out[2:0], bcd_helper_17_out[3]}), .out({bcd_helper_21_out[3], BCD_Output[11:9]}));
  // Probe on BCD_Output[11:8]
  // Probe on BCD_Output[7:4]
  // Probe on {BCD_Output[3:1], _8bit_Input[0]}

  assign BCD_Output[0] = _8bit_Input[0];

  // Notes on the sheet:
  //   The double dable algorithm
endmodule

module bcd_helper (
  input  [3:0] inp,
  output [3:0] out
);

  wire comparator_1_eq, comparator_1_lt, or_1_out;
  wire [3:0] adder_1_out;

  // Probe on inp
  Adder #(.width(4)) adder_1 (.a(4'b0011), .b(inp), .out(adder_1_out));  // open: cin, cout
  Comparator #(.width(4), .mode("unsigned")) comparator_1 (
    .a(4'b0101), .b(inp), .eq(comparator_1_eq), .lt(comparator_1_lt));  // open: gt
  or or_1 (or_1_out, comparator_1_eq, comparator_1_lt);
  Multiplexer #(.width(4)) multiplexer_1 (.in0(inp), .in1(adder_1_out), .out(out), .sel(or_1_out));  // open: en
endmodule
